// Digital circuit 1 Bit Buffer.dig as structural Verilog
module _1_Bit_Buffer (
  input  DATA_IN,
  input  WRITE,
  input  ADDR_LINE,
  output out_4
);

  wire delay_1_out, nfet_1_d;

  assign out_4 = WRITE ? DATA_IN : 1'bz;  // Driver driver_1
  NFET nfet_1 (.G(ADDR_LINE), .D(nfet_1_d), .S(out_4));
  Delay #(.delayTime(5)) delay_1 (.in(nfet_1_d), .out(delay_1_out));
  // also tied to GND on the sheet: delay_1_out

  // Notes on the sheet:
  //   DATA_IN: DATA IN
  //   WRITE: WRITE
  //   ADDR_LINE: ADDR LINE
endmodule
